// Logisim project lab10part2.circ as structural Verilog
module ParityGen (
  input  [3:0] \input ,
  output X2,
  output X1,
  output X0
);

  wire and_1_out, and_2_out, and_3_out, and_4_out, and_5_out, and_6_out, and_7_out, and_8_out, and_9_out,
       not_1_out, not_2_out, not_3_out, not_4_out, not_5_out, not_6_out, not_7_out, not_8_out, or_1_out,
       or_2_out, or_3_out, xor_1_out;

  and and_1 (and_1_out, \input [1], \input [0]);
  not not_1 (not_1_out, \input [0]);
  not not_2 (not_2_out, \input [2]);
  not not_3 (not_3_out, \input [1]);
  not not_4 (not_4_out, \input [0]);
  not not_5 (not_5_out, \input [3]);
  not not_6 (not_6_out, \input [2]);
  not not_7 (not_7_out, \input [3]);
  not not_8 (not_8_out, \input [1]);
  and and_2 (and_2_out, \input [2], \input [3]);
  or or_1 (or_1_out, \input [0], \input [1]);
  or or_2 (or_2_out, \input [2], \input [3]);
  xor xor_1 (xor_1_out, \input [1], \input [3]);
  and and_3 (and_3_out, \input [3], not_2_out);
  or or_3 (or_3_out, not_3_out, not_4_out);
  and and_4 (and_4_out, not_5_out, \input [0], not_6_out);
  and and_5 (and_5_out, not_7_out, \input [2], not_8_out);
  and and_6 (and_6_out, not_1_out, xor_1_out);
  and and_7 (and_7_out, and_3_out, or_3_out);
  and and_8 (and_8_out, and_2_out, or_1_out);
  and and_9 (and_9_out, or_2_out, and_1_out);
  or or_4 (X2, and_8_out, and_9_out);
  or or_5 (X1, and_6_out, and_7_out, and_4_out, and_5_out);

  assign X0 = 1'b0;
endmodule
