// Logisim project lab11part1.circ as structural Verilog: 1 circuit, main circuit main
module main (
  input  [15:0] Write_Data,
  input  [1:0] Write_Register,
  input  [1:0] Read_Register_1,
  input  [1:0] Read_Register_2,
  input  Write_Enable,
  output [15:0] Read_Data_1,
  output [15:0] Read_Data_2
);

  wire clock_1_out, demultiplexer_1_out0, demultiplexer_1_out1, demultiplexer_1_out2, demultiplexer_1_out3;
  wire [15:0] r0_q, r1_q, r2_q, r3_q;

  Clock clock_1 (.out(clock_1_out));
  Demultiplexer #(.select(2), .disabled(0)) demultiplexer_1 (
    .out0(demultiplexer_1_out0), .out1(demultiplexer_1_out1), .out2(demultiplexer_1_out2),
    .out3(demultiplexer_1_out3), .in(Write_Enable), .sel(Write_Register));  // open: en
  Register #(.width(16)) r0 (.D(Write_Data), .en(demultiplexer_1_out0), .Q(r0_q), .clk(clock_1_out));  // open: clr
  Register #(.width(16)) r1 (.D(Write_Data), .en(demultiplexer_1_out1), .Q(r1_q), .clk(clock_1_out));  // open: clr
  Register #(.width(16)) r2 (.D(Write_Data), .en(demultiplexer_1_out2), .Q(r2_q), .clk(clock_1_out));  // open: clr
  Register #(.width(16)) r3 (.D(Write_Data), .en(demultiplexer_1_out3), .Q(r3_q), .clk(clock_1_out));  // open: clr
  Multiplexer #(.select(2), .width(16), .disabled(0), .enable("false")) multiplexer_1 (
    .in0(r0_q), .in1(r1_q), .in2(r2_q), .in3(r3_q), .out(Read_Data_1), .sel(Read_Register_1));
  Multiplexer #(.select(2), .width(16), .disabled(0), .enable("false")) multiplexer_2 (
    .in0(r0_q), .in1(r1_q), .in2(r2_q), .in3(r3_q), .out(Read_Data_2), .sel(Read_Register_2));
endmodule
