// Logisim project lab11part2.circ as structural Verilog: 1 circuit, main circuit main
// 8
module main (
  input  in_1,
  input  in_2
);

  wire and_1_out, button_1_out, clock_1_out, d_ff_1_q;
  wire [7:0] counter_1_q, ram_1_data;

  Clock clock_1 (.out(clock_1_out));
  Counter #(.ongoal("stay")) counter_1 (
    .Q(counter_1_q), .clk(clock_1_out), .clr(button_1_out));  // open: load, D, count, carry
  Button button_1 (.out(button_1_out));
  and and_1 (and_1_out, counter_1_q[0], counter_1_q[1], counter_1_q[2], counter_1_q[3], counter_1_q[4], counter_1_q[5], counter_1_q[6], counter_1_q[7]);
  RAM ram_1 (.addr(counter_1_q), .data(ram_1_data), .clk(clock_1_out), .ld(d_ff_1_q));  // open: sel, clr
  D_Flip_Flop d_ff_1 (.clk(clock_1_out), .D(and_1_out), .Q(d_ff_1_q), .en(in_2));  // open: Qn, preset, reset
  assign ram_1_data = in_1 ? {8{1'b0}} : 8'bz;  // Controlled_Buffer controlled_buffer_1
endmodule
