// Logisim project lab12part1.circ as structural Verilog: 2 circuits, main circuit main
module main (
  input  Input,
  output NewState_2,
  output NewState_1,
  output NewState_0,
  output Output
);

  wire and_2_out, and_3_out, and_4_out, and_5_out, and_6_out, and_7_out, and_8_out, and_9_out, and_10_out,
       and_11_out, clock_1_out, NewState_0_q, NewState_1_q, NewState_2_q, not_1_out, not_2_out, not_3_out,
       not_4_out, not_5_out, not_6_out, not_7_out, not_8_out, not_9_out, not_10_out, not_11_out, not_12_out,
       State_0_q, State_1_q, State_2_q;

  Clock clock_1 (.out(clock_1_out));
  D_Flip_Flop State_2 (.clk(clock_1_out), .D(NewState_2_q), .Q(State_2_q));  // open: Qn, preset, en, reset
  D_Flip_Flop State_1 (.clk(clock_1_out), .D(NewState_1_q), .Q(State_1_q));  // open: Qn, preset, en, reset
  D_Flip_Flop State_0 (.clk(clock_1_out), .D(NewState_0_q), .Q(State_0_q));  // open: Qn, preset, en, reset
  not not_1 (not_1_out, clock_1_out);
  D_Flip_Flop u_NewState_2 (.clk(not_1_out), .D(NewState_2), .Q(NewState_2_q));  // open: Qn, preset, en, reset
  D_Flip_Flop u_NewState_1 (.clk(not_1_out), .D(NewState_1), .Q(NewState_1_q));  // open: Qn, preset, en, reset
  D_Flip_Flop u_NewState_0 (.clk(not_1_out), .D(NewState_0), .Q(NewState_0_q));  // open: Qn, preset, en, reset
  not not_2 (not_2_out, State_1_q);
  not not_3 (not_3_out, State_0_q);
  not not_4 (not_4_out, Input);
  not not_5 (not_5_out, State_2_q);
  not not_6 (not_6_out, Input);
  not not_7 (not_7_out, State_0_q);
  not not_8 (not_8_out, State_2_q);
  not not_9 (not_9_out, State_1_q);
  not not_10 (not_10_out, State_0_q);
  not not_11 (not_11_out, State_1_q);
  not not_12 (not_12_out, State_0_q);
  and and_1 (Output, State_2_q, State_1_q);
  and and_2 (and_2_out, State_1_q, State_0_q, Input);
  and and_3 (and_3_out, State_2_q, not_2_out, not_3_out, not_4_out);
  and and_4 (and_4_out, State_2_q, State_0_q, Input);
  and and_5 (and_5_out, not_5_out, State_0_q, not_6_out);
  and and_6 (and_6_out, State_1_q, not_7_out, Input);
  and and_7 (and_7_out, State_2_q, State_0_q, Input);
  and and_8 (and_8_out, State_2_q, State_1_q);
  and and_9 (and_9_out, not_8_out, not_9_out, Input);
  and and_10 (and_10_out, not_10_out, Input);
  and and_11 (and_11_out, State_2_q, not_11_out, not_12_out);
  or or_1 (NewState_2, and_2_out, and_3_out, and_4_out);
  or or_2 (NewState_1, and_5_out, and_6_out, and_7_out, and_8_out);
  or or_3 (NewState_0, and_9_out, and_10_out, and_11_out);
endmodule

module FSM (
  input  State_2,
  input  State_1,
  input  State_0,
  input  Input,
  output NewState_2,
  output NewState_1,
  output NewState_0,
  output Output
);

  wire and_1_out, and_2_out, and_3_out, and_4_out, and_5_out, and_6_out, and_7_out, and_9_out, and_10_out,
       and_11_out, not_1_out, not_2_out, not_3_out, not_4_out, not_5_out, not_6_out, not_7_out, not_8_out,
       not_9_out, not_10_out, not_11_out;

  not not_1 (not_1_out, State_1);
  not not_2 (not_2_out, State_0);
  not not_3 (not_3_out, Input);
  not not_4 (not_4_out, State_2);
  and and_1 (and_1_out, not_4_out, State_0, not_5_out);
  not not_5 (not_5_out, Input);
  not not_6 (not_6_out, State_0);
  and and_2 (and_2_out, State_1, not_6_out, Input);
  and and_3 (and_3_out, State_2, State_0, Input);
  and and_4 (and_4_out, State_2, State_1);
  not not_7 (not_7_out, State_2);
  not not_8 (not_8_out, State_1);
  and and_5 (and_5_out, not_7_out, not_8_out, Input);
  not not_9 (not_9_out, State_0);
  and and_6 (and_6_out, not_9_out, Input);
  not not_10 (not_10_out, State_1);
  and and_7 (and_7_out, State_2, not_10_out, not_11_out);
  not not_11 (not_11_out, State_0);
  and and_8 (Output, State_2, State_1);
  and and_9 (and_9_out, State_1, State_0, Input);
  and and_10 (and_10_out, State_2, not_1_out, not_2_out, not_3_out);
  or or_1 (NewState_2, and_9_out, and_10_out, and_11_out);
  and and_11 (and_11_out, State_2, State_0, Input);
  or or_2 (NewState_1, and_1_out, and_2_out, and_3_out, and_4_out);
  or or_3 (NewState_0, and_5_out, and_6_out, and_7_out);
endmodule
