// Logisim project CoeMIPS.circ as structural Verilog: 16 circuits, main circuit main
module main (
  input  in_1
);

  wire alu_1_positive_result, alu_1_zero_result, clock_1_out, control_1_branch_control,
       control_1_halt_enable, control_1_led_enable, control_1_load_control, control_1_ram_enable,
       control_1_regwrite_control, control_1_store_control, not_1_out;
  wire [1:0] control_1_alu_source, control_1_jump_control, control_1_register_write_source;
  wire [2:0] control_1_alu_control, instruction_decoder_1_reg1, instruction_decoder_1_reg2;
  wire [3:0] led_decoder_1_hexdigit_0, led_decoder_1_hexdigit_1, led_decoder_1_hexdigit_2,
       led_decoder_1_hexdigit_3;
  wire [7:0] adder_1_out, bit_extender_2_out, bit_extender_3_out, bit_extender_4_out, multiplexer_3_out,
       multiplexer_4_out, PC_q;
  wire [15:0] alu_1_alu_result, bit_extender_1_out, instruction_decoder_1_imm, instruction_decoder_1_shamt,
       multiplexer_1_out, multiplexer_2_out, ram_1_data, register_file_1_read_data_1,
       register_file_1_read_data_2, rom_1_data;

  Register PC (.D(multiplexer_4_out), .en(control_1_halt_enable), .Q(PC_q), .clk(clock_1_out), .clr(in_1));
  not not_1 (not_1_out, control_1_halt_enable);
  LED led_1 (.in(not_1_out));
  Clock clock_1 (.out(clock_1_out));
  Adder adder_1 (.a(PC_q), .b(8'h1), .out(adder_1_out));  // open: cin, cout
  assign bit_extender_1_out = {{8{1'b0}}, adder_1_out};  // Bit_Extender bit_extender_1
  ROM #(.dataWidth(16)) rom_1 (.addr(PC_q), .data(rom_1_data));  // open: sel
  Instruction_Decoder instruction_decoder_1 (
    .Instruction(rom_1_data), .Shamt(instruction_decoder_1_shamt), .Reg2(instruction_decoder_1_reg2),
    .Reg1(instruction_decoder_1_reg1), .IMM(instruction_decoder_1_imm));
  Control control_1 (
    .Instruction(rom_1_data), .Zero_Result(alu_1_zero_result), .Positive_Result(alu_1_positive_result),
    .Load_Control(control_1_load_control), .Store_Control(control_1_store_control),
    .RAM_Enable(control_1_ram_enable), .LED_Enable(control_1_led_enable),
    .Halt_Enable(control_1_halt_enable), .ALU_Source(control_1_alu_source),
    .Jump_Control(control_1_jump_control), .RegWrite_Control(control_1_regwrite_control),
    .Register_Write_Source(control_1_register_write_source), .Branch_Control(control_1_branch_control),
    .ALU_Control(control_1_alu_control));
  Multiplexer #(.select(2), .width(16), .disabled(0), .enable("false")) multiplexer_1 (
    .in0(alu_1_alu_result), .in1(ram_1_data), .in2(bit_extender_1_out), .out(multiplexer_1_out),
    .sel(control_1_register_write_source));  // open: in3
  Register_File register_file_1 (
    .Write_Data(multiplexer_1_out), .Clock(clock_1_out), .RegWrite(control_1_regwrite_control),
    .Read_Data_1(register_file_1_read_data_1), .Read_Data_2(register_file_1_read_data_2),
    .Write_Register(instruction_decoder_1_reg1), .Read_Register_1(instruction_decoder_1_reg1),
    .Read_Register_2(instruction_decoder_1_reg2));
  Bit_Extender #(.in_width(16), .out_width(8)) bit_extender_2 (
    .in(instruction_decoder_1_imm), .out(bit_extender_2_out));
  Bit_Extender #(.in_width(16), .out_width(8)) bit_extender_3 (
    .in(register_file_1_read_data_1), .out(bit_extender_3_out));
  Multiplexer #(.select(2), .width(16), .disabled(0), .enable("false")) multiplexer_2 (
    .in0(register_file_1_read_data_2), .in1(instruction_decoder_1_imm), .in2(instruction_decoder_1_shamt),
    .out(multiplexer_2_out), .sel(control_1_alu_source));  // open: in3
  Multiplexer #(.select(2), .width(8), .disabled(0), .enable("false")) multiplexer_3 (
    .in0(adder_1_out), .in1(bit_extender_2_out), .in2(bit_extender_3_out), .out(multiplexer_3_out),
    .sel(control_1_jump_control));  // open: in3
  ALU alu_1 (
    .A(register_file_1_read_data_1), .B(multiplexer_2_out), .ALU_Result(alu_1_alu_result),
    .Zero_Result(alu_1_zero_result), .ALU_Control(control_1_alu_control),
    .Positive_Result(alu_1_positive_result));
  Bit_Extender #(.in_width(16), .out_width(8)) bit_extender_4 (.in(multiplexer_2_out), .out(bit_extender_4_out));
  LED_Decoder led_decoder_1 (
    .LED_Data(register_file_1_read_data_1), .LED_Control(control_1_led_enable),
    .HexDigit_0(led_decoder_1_hexdigit_0), .HexDigit_1(led_decoder_1_hexdigit_1),
    .HexDigit_2(led_decoder_1_hexdigit_2), .HexDigit_3(led_decoder_1_hexdigit_3), .Clock(clock_1_out));
  Hex_Digit_Display hex_digit_display_1 (.value(led_decoder_1_hexdigit_3));  // open: dp
  Multiplexer #(.width(8), .disabled(0), .enable("false")) multiplexer_4 (
    .in0(multiplexer_3_out), .in1(bit_extender_2_out), .out(multiplexer_4_out), .sel(control_1_branch_control));
  Hex_Digit_Display hex_digit_display_2 (.value(led_decoder_1_hexdigit_2));  // open: dp
  Hex_Digit_Display hex_digit_display_3 (.value(led_decoder_1_hexdigit_0));  // open: dp
  Hex_Digit_Display hex_digit_display_4 (.value(led_decoder_1_hexdigit_1));  // open: dp
  RAM #(.dataWidth(16), .bus("separate")) ram_1 (
    .addr(bit_extender_4_out), .din(register_file_1_read_data_1), .data(ram_1_data),
    .str(control_1_store_control), .sel(control_1_ram_enable), .clk(clock_1_out), .ld(control_1_load_control));  // open: clr

  // Notes on the sheet:
  //   contents of rom_1 (hex, n*v repeats v):
  //   1 f000 1001 241 200 12f0 b201 10ff 481 1503 5008 f000 14ff a40a 1 1108 5018 901 190f 5818 481 1504
  //   f000 6c1 600 3701 5609 30c0 3000 5809 14ff 8421 8e16 7000
  //   Christian Boni
  //   cjb90@pitt.edu
endmodule

module ALU_4Func (
  input  [15:0] A,
  input  [1:0] ALU_Control,
  input  [15:0] B,
  output [15:0] ALU_Result
);

  wire [15:0] adder_1_out, and_1_out, nor_1_out, subtractor_1_out;

  Adder #(.width(16)) adder_1 (.a(A), .b(B), .out(adder_1_out));  // open: cin, cout
  Subtractor #(.width(16)) subtractor_1 (.a(A), .b(B), .out(subtractor_1_out));  // open: bin, bout
  assign and_1_out = A & B;  // AND_Gate and_1, 16 bits wide
  assign nor_1_out = ~(A | B);  // NOR_Gate nor_1, 16 bits wide
  Multiplexer #(.select(2), .width(16), .enable("false")) multiplexer_1 (
    .in0(adder_1_out), .in1(subtractor_1_out), .in2(and_1_out), .in3(nor_1_out), .out(ALU_Result),
    .sel(ALU_Control));
endmodule

module ALU (
  input  [15:0] A,
  input  [15:0] B,
  input  [2:0] ALU_Control,
  output [15:0] ALU_Result,
  output Positive_Result,
  output Zero_Result
);

  wire [15:0] adder_1_out, and_1_out, nor_1_out, shifter_1_out_3, shifter_1_out_4, subtractor_1_out;

  Adder #(.width(16)) adder_1 (.a(A), .b(B), .out(adder_1_out));  // open: cin, cout
  Subtractor #(.width(16)) subtractor_1 (.a(A), .b(B), .out(subtractor_1_out));  // open: bin, bout
  assign and_1_out = A & B;  // AND_Gate and_1, 16 bits wide
  assign nor_1_out = ~(A | B);  // NOR_Gate nor_1, 16 bits wide
  Comparator #(.width(16)) comparator_1 (.a(A), .b({16{1'b0}}), .gt(Positive_Result), .eq(Zero_Result));  // open: lt
  Shifter shifter_1 (.Shift_Data(A), .Shift_Amount(B), .out_3(shifter_1_out_3), .out_4(shifter_1_out_4));
  Multiplexer #(.select(3), .width(16), .disabled(0), .enable("false")) multiplexer_1 (
    .in0(adder_1_out), .in1(subtractor_1_out), .in2(and_1_out), .in3(nor_1_out), .in4(shifter_1_out_3),
    .in5(shifter_1_out_4), .out(ALU_Result), .sel(ALU_Control));  // open: in6, in7
endmodule

module Register_File (
  input  [2:0] Write_Register,
  input  [15:0] Write_Data,
  input  [2:0] Read_Register_1,
  input  [2:0] Read_Register_2,
  input  Clock,
  input  RegWrite,
  output [15:0] Read_Data_1,
  output [15:0] Read_Data_2
);

  wire demultiplexer_1_out0, demultiplexer_1_out1, demultiplexer_1_out2, demultiplexer_1_out3,
       demultiplexer_1_out4, demultiplexer_1_out5, demultiplexer_1_out6, demultiplexer_1_out7;
  wire [15:0] r0_q, r1_q, r2_q, r3_q, r4_q, r5_q, r6_q, r7_q;

  Demultiplexer #(.select(3), .disabled(0)) demultiplexer_1 (
    .out0(demultiplexer_1_out0), .out1(demultiplexer_1_out1), .out2(demultiplexer_1_out2),
    .out3(demultiplexer_1_out3), .out4(demultiplexer_1_out4), .out5(demultiplexer_1_out5),
    .out6(demultiplexer_1_out6), .out7(demultiplexer_1_out7), .in(RegWrite), .sel(Write_Register),
    .en(RegWrite));
  Register #(.width(16)) r0 (.D(Write_Data), .en(demultiplexer_1_out0), .Q(r0_q), .clk(Clock));  // open: clr
  Register #(.width(16)) r1 (.D(Write_Data), .en(demultiplexer_1_out1), .Q(r1_q), .clk(Clock));  // open: clr
  Register #(.width(16)) r2 (.D(Write_Data), .en(demultiplexer_1_out2), .Q(r2_q), .clk(Clock));  // open: clr
  Register #(.width(16)) r3 (.D(Write_Data), .en(demultiplexer_1_out3), .Q(r3_q), .clk(Clock));  // open: clr
  Register #(.width(16)) r5 (.D(Write_Data), .en(demultiplexer_1_out5), .Q(r5_q), .clk(Clock));  // open: clr
  Register #(.width(16)) r4 (.D(Write_Data), .en(demultiplexer_1_out4), .Q(r4_q), .clk(Clock));  // open: clr
  Register #(.width(16)) r6 (.D(Write_Data), .en(demultiplexer_1_out6), .Q(r6_q), .clk(Clock));  // open: clr
  Register #(.width(16)) r7 (.D(Write_Data), .en(demultiplexer_1_out7), .Q(r7_q), .clk(Clock));  // open: clr
  Multiplexer #(.select(3), .width(16), .disabled(0), .enable("false")) multiplexer_1 (
    .in0(r0_q), .in1(r1_q), .in2(r2_q), .in3(r3_q), .in4(r4_q), .in5(r5_q), .in6(r6_q), .in7(r7_q),
    .out(Read_Data_1), .sel(Read_Register_1));
  Multiplexer #(.select(3), .width(16), .disabled(0), .enable("false")) multiplexer_2 (
    .in0(r0_q), .in1(r1_q), .in2(r2_q), .in3(r3_q), .in4(r4_q), .in5(r5_q), .in6(r6_q), .in7(r7_q),
    .out(Read_Data_2), .sel(Read_Register_2));
endmodule

module LED_Decoder (
  input  [15:0] LED_Data,
  input  LED_Control,
  input  Clock,
  output [3:0] HexDigit_0,
  output [3:0] HexDigit_1,
  output [3:0] HexDigit_2,
  output [3:0] HexDigit_3
);

  Register #(.width(16)) register_1 (
    .D(LED_Data), .en(LED_Control), .Q({HexDigit_3, HexDigit_2, HexDigit_1, HexDigit_0}), .clk(Clock));  // open: clr
endmodule

module Shifter (
  input  [15:0] Shift_Data,
  input  [15:0] Shift_Amount,
  output [15:0] out_3,
  output [15:0] out_4
);

  wire [3:0] bit_extender_1_out;

  Bit_Extender #(.in_width(16), .out_width(4)) bit_extender_1 (.in(Shift_Amount), .out(bit_extender_1_out));
  Shifter_part #(.width(16)) shifter_1 (.in(Shift_Data), .\dist (bit_extender_1_out), .out(out_3));
  Shifter_part #(.width(16), .shift("lr")) shifter_2 (.in(Shift_Data), .\dist (bit_extender_1_out), .out(out_4));
endmodule

module Instruction_Decoder (
  input  [15:0] Instruction,
  output [15:0] Shamt,
  output [2:0] Reg2,
  output [2:0] Reg1,
  output [15:0] IMM
);

  wire and_1_out, not_1_out, not_2_out, not_3_out, not_4_out;
  wire [15:0] bit_extender_2_out, bit_extender_3_out;

  not not_1 (not_1_out, Instruction[8]);
  not not_2 (not_2_out, Instruction[13]);
  not not_3 (not_3_out, Instruction[14]);
  not not_4 (not_4_out, Instruction[15]);
  assign Shamt = {{12{1'b0}}, Instruction[4:1]};  // Bit_Extender bit_extender_1
  assign bit_extender_2_out = {{8{1'b0}}, Instruction[7:0]};  // Bit_Extender bit_extender_2
  assign bit_extender_3_out = {{8{Instruction[7]}}, Instruction[7:0]};  // Bit_Extender bit_extender_3
  and and_1 (and_1_out, not_1_out, Instruction[12], not_2_out, not_3_out, not_4_out);
  Multiplexer #(.width(16), .disabled(0), .enable("false")) multiplexer_1 (
    .in0(bit_extender_2_out), .in1(bit_extender_3_out), .out(IMM), .sel(and_1_out));

  assign Reg1 = Instruction[11:9];
  assign Reg2 = Instruction[8:6];
endmodule

module Control (
  input  [15:0] Instruction,
  input  Zero_Result,
  input  Positive_Result,
  output Load_Control,
  output Store_Control,
  output RAM_Enable,
  output LED_Enable,
  output Halt_Enable,
  output [1:0] ALU_Source,
  output [1:0] Jump_Control,
  output RegWrite_Control,
  output [1:0] Register_Write_Source,
  output Branch_Control,
  output [2:0] ALU_Control
);

  wire and_4_out, Branch_Control__Positive_branch_control1, Branch_Control__Zero_branch_control0, not_1_out,
       not_2_out;

  Memory_Enable Memory_Enable (
    .Op_Code0(Instruction[12]), .Op_Code1(Instruction[13]), .Op_Code2(Instruction[14]),
    .Op_Code3(Instruction[15]), .Memory_Enable(RAM_Enable));
  ALU_Source u_ALU_Source (
    .Op_Code3(Instruction[15]), .Op_Code2(Instruction[14]), .Op_Code1(Instruction[13]),
    .Op_Code0(Instruction[12]), .ALU_Source1(ALU_Source[1]), .ALU_Source0(ALU_Source[0]));
  Jump_Control u_Jump_Control (
    .Op_Code3(Instruction[15]), .Op_Code2(Instruction[14]), .Op_Code1(Instruction[13]),
    .Op_Code0(Instruction[12]), .Jump1(Jump_Control[1]), .Jump0(Jump_Control[0]));
  not not_1 (not_1_out, Instruction[0]);
  not not_2 (not_2_out, Instruction[15]);
  RegWrite_Control u_RegWrite_Control (
    .Op_Code3(Instruction[15]), .Op_Code2(Instruction[14]), .Op_Code1(Instruction[13]),
    .Op_Code0(Instruction[12]), .SubOp(Instruction[0]), .RegWrite_Control(RegWrite_Control));
  Register_Write_Source u_Register_Write_Source (
    .Op_Code3(Instruction[15]), .Op_Code2(Instruction[14]), .Op_Code1(Instruction[13]),
    .Op_Code0(Instruction[12]), .RegisterWrite_Source1(Register_Write_Source[1]),
    .RegisterWriteSource0(Register_Write_Source[0]));
  Branch_Control__Zero Branch_Control__Zero (
    .OpCode3(Instruction[15]), .OpCode2(Instruction[14]), .OpCode1(Instruction[13]),
    .OpCode0(Instruction[12]), .Zero_Result(Zero_Result),
    .Branch_Control0(Branch_Control__Zero_branch_control0));
  Branch_Control__positive Branch_Control__Positive (
    .OpCode3(Instruction[15]), .OpCode2(Instruction[14]), .OpCode1(Instruction[13]),
    .OpCode0(Instruction[12]), .Positive_Result(Positive_Result),
    .Branch_Control1(Branch_Control__Positive_branch_control1), .Zero_Result(Zero_Result));
  ALU_Control u_ALU_Control (
    .OpCode3(Instruction[15]), .OpCode2(Instruction[14]), .OpCode1(Instruction[13]),
    .OpCode0(Instruction[12]), .SubOp(Instruction[0]), .ALU_Control2(ALU_Control[2]),
    .ALU_Control1(ALU_Control[1]), .ALU_Contro0(ALU_Control[0]));
  and and_1 (Load_Control, not_1_out, RAM_Enable);
  and and_2 (Store_Control, Instruction[0], RAM_Enable);
  and and_3 (LED_Enable, Instruction[12], Instruction[13], Instruction[14], Instruction[15]);
  and and_4 (and_4_out, Instruction[12], Instruction[13], Instruction[14], not_2_out);
  or or_1 (Branch_Control, Branch_Control__Zero_branch_control0, Branch_Control__Positive_branch_control1);
  not not_3 (Halt_Enable, and_4_out);
endmodule

module Memory_Enable (
  input  Op_Code0,
  input  Op_Code1,
  input  Op_Code2,
  input  Op_Code3,
  output Memory_Enable
);

  wire not_1_out, not_2_out;

  not not_1 (not_1_out, Op_Code0);
  not not_2 (not_2_out, Op_Code3);
  and and_1 (Memory_Enable, not_1_out, Op_Code1, Op_Code2, not_2_out);
endmodule

module ALU_Source (
  input  Op_Code3,
  input  Op_Code2,
  input  Op_Code1,
  input  Op_Code0,
  output ALU_Source1,
  output ALU_Source0
);

  wire and_1_out, and_2_out, and_3_out, not_1_out, not_2_out, not_3_out, not_4_out, not_5_out;

  not not_1 (not_1_out, Op_Code3);
  not not_2 (not_2_out, Op_Code1);
  not not_3 (not_3_out, Op_Code2);
  and and_1 (and_1_out, not_3_out, not_4_out, Op_Code0);
  not not_4 (not_4_out, Op_Code1);
  and and_2 (and_2_out, Op_Code3, not_5_out);
  not not_5 (not_5_out, Op_Code0);
  and and_3 (and_3_out, Op_Code3, Op_Code1);
  and and_4 (ALU_Source1, not_1_out, Op_Code2, not_2_out, Op_Code0);
  or or_1 (ALU_Source0, and_1_out, and_2_out, and_3_out);
endmodule

module Jump_Control (
  input  Op_Code3,
  input  Op_Code2,
  input  Op_Code1,
  input  Op_Code0,
  output Jump1,
  output Jump0
);

  wire not_1_out, not_2_out;

  not not_1 (not_1_out, Op_Code1);
  and and_1 (Jump0, Op_Code3, Op_Code2, not_2_out);
  not not_2 (not_2_out, Op_Code0);
  and and_2 (Jump1, Op_Code3, Op_Code2, not_1_out, Op_Code0);
endmodule

module RegWrite_Control (
  input  Op_Code3,
  input  Op_Code2,
  input  Op_Code1,
  input  Op_Code0,
  input  SubOp,
  output RegWrite_Control
);

  wire and_1_out, and_2_out, and_3_out, and_4_out, not_1_out, not_2_out, not_3_out, not_4_out, not_5_out,
       not_6_out, not_7_out, not_8_out, not_9_out;

  not not_1 (not_1_out, Op_Code3);
  not not_2 (not_2_out, Op_Code2);
  not not_3 (not_3_out, Op_Code3);
  not not_4 (not_4_out, Op_Code1);
  not not_5 (not_5_out, Op_Code3);
  not not_6 (not_6_out, Op_Code0);
  not not_7 (not_7_out, SubOp);
  not not_8 (not_8_out, Op_Code1);
  not not_9 (not_9_out, Op_Code0);
  and and_1 (and_1_out, not_1_out, not_2_out);
  and and_2 (and_2_out, not_3_out, not_4_out);
  and and_3 (and_3_out, not_5_out, not_6_out, not_7_out);
  and and_4 (and_4_out, Op_Code2, not_8_out, not_9_out);
  or or_1 (RegWrite_Control, and_1_out, and_2_out, and_3_out, and_4_out);
endmodule

module Register_Write_Source (
  input  Op_Code3,
  input  Op_Code2,
  input  Op_Code1,
  input  Op_Code0,
  output RegisterWrite_Source1,
  output RegisterWriteSource0
);

  and and_1 (RegisterWriteSource0, Op_Code2, Op_Code1);

  assign RegisterWrite_Source1 = Op_Code3;
endmodule

module Branch_Control__Zero (
  input  OpCode3,
  input  OpCode2,
  input  OpCode1,
  input  OpCode0,
  input  Zero_Result,
  output Branch_Control0
);

  wire and_1_out, and_2_out, not_1_out, not_2_out, not_3_out, not_4_out, not_5_out, not_6_out;

  not not_1 (not_1_out, OpCode2);
  not not_2 (not_2_out, OpCode1);
  not not_3 (not_3_out, OpCode0);
  not not_4 (not_4_out, OpCode2);
  not not_5 (not_5_out, OpCode1);
  not not_6 (not_6_out, Zero_Result);
  and and_1 (and_1_out, OpCode3, not_1_out, not_2_out, not_3_out, Zero_Result);
  and and_2 (and_2_out, OpCode3, not_4_out, not_5_out, OpCode0, not_6_out);
  or or_1 (Branch_Control0, and_1_out, and_2_out);
endmodule

module Branch_Control__positive (
  input  OpCode3,
  input  OpCode2,
  input  OpCode1,
  input  OpCode0,
  input  Positive_Result,
  input  Zero_Result,
  output Branch_Control1
);

  wire and_1_out, and_2_out, not_1_out, not_2_out, not_3_out, not_4_out, not_5_out, or_1_out;

  not not_1 (not_1_out, OpCode2);
  not not_2 (not_2_out, OpCode0);
  not not_3 (not_3_out, OpCode2);
  not not_4 (not_4_out, Positive_Result);
  not not_5 (not_5_out, Zero_Result);
  and and_1 (and_1_out, OpCode3, not_1_out, OpCode1, not_2_out, Positive_Result);
  and and_2 (and_2_out, OpCode3, not_3_out, OpCode1, OpCode0, not_4_out);
  or or_1 (or_1_out, and_1_out, and_2_out);
  and and_3 (Branch_Control1, or_1_out, not_5_out);
endmodule

module ALU_Control (
  input  OpCode3,
  input  OpCode2,
  input  OpCode1,
  input  OpCode0,
  input  SubOp,
  output ALU_Control2,
  output ALU_Control1,
  output ALU_Contro0
);

  wire and_1_out, and_2_out, and_3_out, not_1_out, not_2_out;

  not not_1 (not_1_out, OpCode0);
  not not_2 (not_2_out, SubOp);
  and and_1 (and_1_out, not_1_out, SubOp);
  and and_2 (and_2_out, OpCode1, not_2_out);
  and and_3 (and_3_out, OpCode2, SubOp);
  or or_1 (ALU_Contro0, and_1_out, and_2_out, and_3_out);

  assign ALU_Control1 = OpCode1;
  assign ALU_Control2 = OpCode2;
endmodule
